// Logisim project PROJETO CD -TESTE.circ as structural Verilog: 16 circuits, main circuit main
module main (
  input  ENABLE,
  input  CLEAR,
  input  CONF
);

  wire CLK_out, \CRÔNOMETRO_out_13 , DMA_out, DSA_out, UMA_out, USA_out;
  wire [3:0] \CRÔNOMETRO_c0 , \CRÔNOMETRO_c1 , \CRÔNOMETRO_c2 , \CRÔNOMETRO_c3 , decodificador_1_inferior,
       decodificador_1_superior, decodificador_2_inferior, decodificador_2_superior,
       decodificador_3_inferior, decodificador_3_superior, decodificador_4_inferior, decodificador_4_superior;

  Clock CLK (.out(CLK_out));
  Button DMA (.out(DMA_out));
  \CRÔNOMETRO  \CRÔNOMETRO  (
    .ENABLE(ENABLE), .CLEAR(CLEAR), .CLK(CLK_out), .CONF(CONF), .C3(\CRÔNOMETRO_c3 ), .C2(\CRÔNOMETRO_c2 ),
    .C1(\CRÔNOMETRO_c1 ), .C0(\CRÔNOMETRO_c0 ), .in_1(DMA_out), .in_2(UMA_out), .in_3(DSA_out),
    .in_4(USA_out), .out_13(\CRÔNOMETRO_out_13 ));
  LED led_1 (.in(CONF));
  Button USA (.out(USA_out));
  Button UMA (.out(UMA_out));
  Button DSA (.out(DSA_out));
  DECODIFICADOR decodificador_1 (
    .in_1(\CRÔNOMETRO_c3 ), .SUPERIOR(decodificador_1_superior), .INFERIOR(decodificador_1_inferior));
  _7_Segment_Display u_7_segment_display_1 (
    .g(decodificador_1_superior[3]), .f(decodificador_1_superior[2]), .a(decodificador_1_superior[1]),
    .b(decodificador_1_superior[0]), .e(decodificador_1_inferior[3]), .d(decodificador_1_inferior[2]),
    .c(decodificador_1_inferior[1]), .dp(decodificador_1_inferior[0]));
  DECODIFICADOR decodificador_2 (
    .in_1(\CRÔNOMETRO_c2 ), .SUPERIOR(decodificador_2_superior), .INFERIOR(decodificador_2_inferior));
  _7_Segment_Display u_7_segment_display_2 (
    .g(decodificador_2_superior[3]), .f(decodificador_2_superior[2]), .a(decodificador_2_superior[1]),
    .b(decodificador_2_superior[0]), .e(decodificador_2_inferior[3]), .d(decodificador_2_inferior[2]),
    .c(decodificador_2_inferior[1]), .dp(decodificador_2_inferior[0]));
  DECODIFICADOR decodificador_3 (
    .in_1(\CRÔNOMETRO_c1 ), .SUPERIOR(decodificador_3_superior), .INFERIOR(decodificador_3_inferior));
  DECODIFICADOR decodificador_4 (
    .in_1(\CRÔNOMETRO_c0 ), .SUPERIOR(decodificador_4_superior), .INFERIOR(decodificador_4_inferior));
  _7_Segment_Display u_7_segment_display_3 (
    .g(decodificador_4_superior[3]), .f(decodificador_4_superior[2]), .a(decodificador_4_superior[1]),
    .b(decodificador_4_superior[0]), .e(decodificador_4_inferior[3]), .d(decodificador_4_inferior[2]),
    .c(decodificador_4_inferior[1]), .dp(decodificador_4_inferior[0]));
  _7_Segment_Display u_7_segment_display_4 (
    .g(decodificador_3_superior[3]), .f(decodificador_3_superior[2]), .a(decodificador_3_superior[1]),
    .b(decodificador_3_superior[0]), .e(decodificador_3_inferior[3]), .d(decodificador_3_inferior[2]),
    .c(decodificador_3_inferior[1]), .dp(decodificador_3_inferior[0]));
  LED \CRÔNOMETRO_ZERADO  (.in(\CRÔNOMETRO_out_13 ));
endmodule

// 5-0
module CONTDEC (
  input  CONF,
  input  CLK,
  input  CLEAR,
  input  ENABLE,
  output [3:0] out_5,
  output out_6
);

  wire conversor_05_1_q0, conversor_05_1_q1, conversor_05_1_q2, conversor_05_1_q3, xor_1_out;

  xor xor_1 (xor_1_out, CONF, CLK);
  D_Flip_Flop #(.trigger("falling")) d_ff_1 (
    .clk(xor_1_out), .D(conversor_05_1_q0), .Q(out_5[3]), .en(ENABLE), .reset(CLEAR));  // open: Qn, preset
  D_Flip_Flop #(.trigger("falling")) d_ff_2 (
    .clk(xor_1_out), .D(conversor_05_1_q1), .Q(out_5[2]), .en(ENABLE), .reset(CLEAR));  // open: Qn, preset
  CONVERSOR_05 conversor_05_1 (
    .D0(out_5[3]), .D1(out_5[2]), .D2(out_5[1]), .D3(out_5[0]), .Q0(conversor_05_1_q0),
    .Q1(conversor_05_1_q1), .Q2(conversor_05_1_q2), .Q3(conversor_05_1_q3), .SS(out_6));
  D_Flip_Flop #(.trigger("falling")) d_ff_3 (
    .clk(xor_1_out), .D(conversor_05_1_q2), .Q(out_5[1]), .en(ENABLE), .reset(CLEAR));  // open: Qn, preset
  Hex_Digit_Display hex_digit_display_1 (.value(out_5));  // open: dp
  D_Flip_Flop #(.trigger("falling")) d_ff_4 (
    .clk(xor_1_out), .D(conversor_05_1_q3), .Q(out_5[0]), .en(ENABLE), .reset(CLEAR));  // open: Qn, preset
endmodule

// 9-0
module CONTUNI (
  input  CONF,
  input  CLK,
  input  CLEAR,
  input  ENABLE,
  output [3:0] out_5,
  output out_6
);

  wire conversor_09_1_q0, conversor_09_1_q1, conversor_09_1_q2, conversor_09_1_q3, xor_1_out;

  xor xor_1 (xor_1_out, CONF, CLK);
  D_Flip_Flop #(.trigger("falling")) d_ff_1 (
    .clk(xor_1_out), .D(conversor_09_1_q0), .Q(out_5[3]), .en(ENABLE), .reset(CLEAR));  // open: Qn, preset
  D_Flip_Flop #(.trigger("falling")) d_ff_2 (
    .clk(xor_1_out), .D(conversor_09_1_q1), .Q(out_5[2]), .en(ENABLE), .reset(CLEAR));  // open: Qn, preset
  CONVERSOR_09 conversor_09_1 (
    .D0(out_5[3]), .D1(out_5[2]), .D2(out_5[1]), .D3(out_5[0]), .Q0(conversor_09_1_q0),
    .Q1(conversor_09_1_q1), .Q2(conversor_09_1_q2), .Q3(conversor_09_1_q3), .SS(out_6));
  D_Flip_Flop #(.trigger("falling")) d_ff_3 (
    .clk(xor_1_out), .D(conversor_09_1_q2), .Q(out_5[1]), .en(ENABLE), .reset(CLEAR));  // open: Qn, preset
  Hex_Digit_Display hex_digit_display_1 (.value(out_5));  // open: dp
  D_Flip_Flop #(.trigger("falling")) d_ff_4 (
    .clk(xor_1_out), .D(conversor_09_1_q3), .Q(out_5[0]), .en(ENABLE), .reset(CLEAR));  // open: Qn, preset
endmodule

module CONVERSOR_09 (
  input  D0,
  input  D1,
  input  D2,
  input  D3,
  output Q0,
  output Q1,
  output Q2,
  output Q3,
  output SS
);

  wire and_1_out, and_2_out, and_3_out, and_4_out, and_5_out, and_6_out, and_7_out, and_8_out;

  and and_1 (and_1_out, ~D0, ~D1, ~D2, ~D3);  // AND_Gate
  and and_2 (and_2_out, D0, D3);
  and and_3 (and_3_out, D1, D3);
  and and_4 (and_4_out, D1, D2);
  and and_5 (and_5_out, D0, ~D3);  // AND_Gate
  and and_6 (and_6_out, D2, D3);
  and and_7 (and_7_out, D1, ~D2, ~D3);  // AND_Gate
  and and_8 (and_8_out, D0, ~D3);  // AND_Gate
  not not_1 (Q3, D3);
  and and_9 (SS, ~D0, ~D1, ~D2, ~D3);  // AND_Gate
  or or_1 (Q0, and_1_out, and_2_out);
  or or_2 (Q1, and_3_out, and_4_out, and_5_out);
  or or_3 (Q2, and_6_out, and_7_out, and_8_out);
endmodule

module CONVERSOR_05 (
  input  D0,
  input  D1,
  input  D2,
  input  D3,
  output Q0,
  output Q1,
  output Q2,
  output Q3,
  output SS
);

  wire and_1_out, and_2_out, and_3_out, and_4_out, not_1_out, not_2_out, not_3_out, not_4_out, not_6_out,
       not_7_out, not_8_out;

  not not_1 (not_1_out, D1);
  not not_2 (not_2_out, D2);
  and and_1 (and_1_out, not_1_out, not_2_out, not_3_out);
  not not_3 (not_3_out, D3);
  and and_2 (and_2_out, D1, D3);
  and and_3 (and_3_out, D2, D3);
  and and_4 (and_4_out, D1, not_4_out);
  not not_4 (not_4_out, D3);
  not not_5 (Q3, D3);
  not not_6 (not_6_out, D1);
  and and_5 (SS, not_6_out, not_7_out, not_8_out);
  not not_7 (not_7_out, D2);
  not not_8 (not_8_out, D3);
  or or_1 (Q1, and_1_out, and_2_out);
  or or_2 (Q2, and_3_out, and_4_out);

  assign Q0 = 1'b0;
endmodule

module DECODIFICADOR (
  input  [3:0] in_1,
  output [3:0] SUPERIOR,
  output [3:0] INFERIOR
);

  wire and_1_out, and_2_out, and_3_out, and_4_out, and_5_out, and_6_out, and_7_out, and_8_out, and_9_out,
       and_10_out, and_11_out, and_12_out, and_13_out, and_14_out, and_15_out, and_16_out, and_17_out,
       and_18_out, and_19_out, and_20_out, and_22_out, and_23_out, and_24_out, nand_1_out, nor_1_out,
       nor_2_out, nor_3_out, nor_4_out, nor_5_out, or_1_out, or_2_out, or_3_out, or_4_out, or_5_out,
       or_6_out, or_7_out, or_8_out, xor_1_out, xor_2_out, xor_3_out;

  or or_1 (or_1_out, in_1[3], ~in_1[2]);  // OR_Gate
  or or_2 (or_2_out, ~in_1[3], in_1[2]);  // OR_Gate
  and and_1 (and_1_out, ~in_1[3], in_1[2], in_1[0]);  // AND_Gate
  and and_2 (and_2_out, in_1[3], ~in_1[2], ~in_1[1]);  // AND_Gate
  xor xor_1 (xor_1_out, in_1[3], in_1[1]);
  nand nand_1 (nand_1_out, in_1[3], in_1[0]);
  nor nor_1 (nor_1_out, in_1[3], in_1[1], in_1[0]);
  and and_3 (and_3_out, ~in_1[1], in_1[0]);  // AND_Gate
  xor xor_2 (xor_2_out, in_1[3], in_1[2]);
  and and_4 (and_4_out, in_1[1], in_1[0]);
  nor nor_2 (nor_2_out, in_1[1], in_1[0]);
  and and_5 (and_5_out, in_1[2], in_1[0]);
  nor nor_3 (nor_3_out, in_1[2], in_1[0]);
  nor nor_4 (nor_4_out, in_1[3], in_1[2]);
  xor xor_3 (xor_3_out, in_1[2], in_1[0]);
  or or_3 (or_3_out, ~in_1[2], in_1[1]);  // OR_Gate
  or or_4 (or_4_out, in_1[2], in_1[1]);
  and and_6 (and_6_out, in_1[3], in_1[1]);
  and and_7 (and_7_out, in_1[3], ~in_1[2]);  // AND_Gate
  nor nor_5 (nor_5_out, in_1[1], in_1[0]);
  and and_8 (and_8_out, in_1[2], ~in_1[0]);  // AND_Gate
  and and_9 (and_9_out, ~in_1[1], in_1[2], ~in_1[3]);  // AND_Gate
  and and_10 (and_10_out, in_1[1], ~in_1[0]);  // AND_Gate
  and and_11 (and_11_out, in_1[3], ~in_1[2]);  // AND_Gate
  and and_12 (and_12_out, in_1[3], in_1[0]);
  and and_13 (and_13_out, ~in_1[3], in_1[2], ~in_1[1]);  // AND_Gate
  and and_14 (and_14_out, ~in_1[2], in_1[1], in_1[0]);  // AND_Gate
  or or_5 (or_5_out, in_1[2], in_1[1]);
  and and_15 (and_15_out, or_1_out, ~in_1[0]);  // AND_Gate
  and and_16 (and_16_out, in_1[1], or_2_out);
  and and_17 (and_17_out, xor_1_out, in_1[0]);
  and and_18 (and_18_out, nand_1_out, ~in_1[2]);  // AND_Gate
  or or_6 (or_6_out, and_4_out, nor_2_out);
  or or_7 (or_7_out, and_5_out, in_1[3], nor_3_out);
  or or_8 (or_8_out, nor_4_out, xor_3_out);
  and and_19 (and_19_out, ~in_1[0], or_3_out);  // AND_Gate
  or E (INFERIOR[3], and_19_out, and_20_out);
  and and_20 (and_20_out, or_4_out, in_1[3]);
  or F (SUPERIOR[2], and_6_out, and_7_out, nor_5_out, and_8_out, and_9_out);
  or G (SUPERIOR[3], and_10_out, and_11_out, and_12_out, and_13_out, and_14_out);
  and and_21 (INFERIOR[0], in_1[3], or_5_out);
  or A (SUPERIOR[1], and_15_out, and_16_out, and_1_out, and_2_out);
  or B (SUPERIOR[0], and_17_out, and_18_out, nor_1_out);
  or C (INFERIOR[1], and_3_out, xor_2_out, and_22_out);
  and and_22 (and_22_out, or_6_out, ~in_1[3]);  // AND_Gate
  and and_23 (and_23_out, or_7_out, ~in_1[1]);  // AND_Gate
  or D (INFERIOR[2], and_23_out, and_24_out);
  and and_24 (and_24_out, in_1[1], or_8_out);
endmodule

module \CRÔNOMETRO  (
  input  in_1,
  input  in_2,
  input  in_3,
  input  in_4,
  input  ENABLE,
  input  CLEAR,
  input  CLK,
  input  CONF,
  output [3:0] C3,
  output [3:0] C2,
  output [3:0] C1,
  output [3:0] C0,
  output out_13
);

  wire and_2_out, and_3_out, and_4_out, and_5_out, contdec_1_out_6, contdec_2_out_6, contuni_1_out_6,
       contuni_2_out_6, xor_1_out;
  wire [3:0] and_9_out;

  and and_1 (out_13, and_3_out, and_4_out, and_5_out, contdec_1_out_6);
  xor xor_1 (xor_1_out, out_13, ENABLE);
  and and_2 (and_2_out, CLK, ~CONF);  // AND_Gate
  Hex_Digit_Display hex_digit_display_1 (.value(C3));  // open: dp
  CONTDEC contdec_1 (
    .out_6(contdec_1_out_6), .CLK(and_3_out), .CLEAR(CLEAR), .ENABLE(xor_1_out), .out_5(C3),
    .CONF(and_9_out[3]));
  Hex_Digit_Display hex_digit_display_2 (.value(C1));  // open: dp
  Hex_Digit_Display hex_digit_display_3 (.value(C2));  // open: dp
  CONTUNI contuni_1 (
    .out_6(contuni_1_out_6), .CLK(and_4_out), .CLEAR(CLEAR), .ENABLE(xor_1_out), .out_5(C2),
    .CONF(and_9_out[2]));
  Hex_Digit_Display hex_digit_display_4 (.value(C0));  // open: dp
  CONTDEC contdec_2 (
    .out_6(contdec_2_out_6), .CLK(and_5_out), .CLEAR(CLEAR), .ENABLE(xor_1_out), .out_5(C1),
    .CONF(and_9_out[1]));
  and and_3 (and_3_out, ~CONF, contuni_1_out_6);  // AND_Gate
  and and_4 (and_4_out, ~CONF, contdec_2_out_6);  // AND_Gate
  and and_5 (and_5_out, ~CONF, contuni_2_out_6);  // AND_Gate
  CONTUNI contuni_2 (
    .out_6(contuni_2_out_6), .CLK(and_2_out), .CLEAR(CLEAR), .ENABLE(xor_1_out), .out_5(C0),
    .CONF(and_9_out[0]));
  and and_6 (and_9_out[3], in_1, CONF);
  and and_7 (and_9_out[2], in_2, CONF);
  and and_8 (and_9_out[1], in_3, CONF);
  and and_9 (and_9_out[0], in_4, CONF);
endmodule

module CORE (
  input  CHUTE,
  input  [3:0] in_2,
  input  PROXIMO,
  input  CLEAR
);

  wire \botão_1_clk , \botão_1_q0 , \botão_1_q1 ;
  wire [2:0] comparador_3_out_3;
  wire [3:0] \variável_1_out_6 , \variável_2_out_6 ;
  wire [4:0] passarchute_1_out_6, passarchute_1_out_7, somador_1_out_3, somador_2_out_3, \variável_1_out_5 ,
       \variável_2_out_5 ;

  \BOTÃO  \botão_1  (.PROXIMO(PROXIMO), .CLK(\botão_1_clk ), .Q0(\botão_1_q0 ), .Q1(\botão_1_q1 ));
  Hex_Digit_Display hex_digit_display_1 (.value(\variável_1_out_6 ));  // open: dp
  \VARIÁVEL  \variável_1  (
    .in_1(in_2), .CLK(\botão_1_clk ), .CLEAR(CLEAR), .ENABLE(\botão_1_q1 ), .out_5(\variável_1_out_5 ),
    .out_6(\variável_1_out_6 ));
  Hex_Digit_Display hex_digit_display_2 (.value(\variável_2_out_6 ));  // open: dp
  \VARIÁVEL  \variável_2  (
    .in_1(in_2), .CLK(\botão_1_clk ), .CLEAR(CLEAR), .ENABLE(\botão_1_q0 ), .out_5(\variável_2_out_5 ),
    .out_6(\variável_2_out_6 ));
  COMPARADOR comparador_1 (.CHUTE(passarchute_1_out_6), .in_1(5'b00011));  // open: out_3
  passarChute passarchute_1 (
    .ENABLE(1'b1), .CLK(CHUTE), .CLEAR(CLEAR), .in_4(\variável_2_out_5 ), .in_5(\variável_1_out_5 ),
    .out_6(passarchute_1_out_6), .out_7(passarchute_1_out_7));
  COMPARADOR comparador_2 (.CHUTE(passarchute_1_out_7), .in_1(5'b00100));  // open: out_3
  SOMADOR somador_1 (.in_1(5'b00011), .in_2(5'b00100), .out_3(somador_1_out_3));
  COMPARADOR comparador_3 (.CHUTE(somador_2_out_3), .in_1(somador_1_out_3), .out_3(comparador_3_out_3));
  SOMADOR somador_2 (.in_1(passarchute_1_out_6), .in_2(passarchute_1_out_7), .out_3(somador_2_out_3));
  LED led_1 (.in(comparador_3_out_3[0]));
  LED led_2 (.in(comparador_3_out_3[1]));
  LED led_3 (.in(comparador_3_out_3[2]));
endmodule

module MULTPLEXADOR (
  input  [3:0] in_1,
  input  [3:0] in_2,
  input  in_3,
  output [3:0] out_4
);

  wire [3:0] and_1_out, and_5_out;

  and and_1 (and_1_out[0], in_1[0], in_3);
  and and_2 (and_1_out[1], in_1[1], in_3);
  and and_3 (and_1_out[2], in_1[2], in_3);
  and and_4 (and_1_out[3], in_1[3], in_3);
  and and_5 (and_5_out[0], ~in_3, in_2[0]);  // AND_Gate
  and and_6 (and_5_out[1], ~in_3, in_2[1]);  // AND_Gate
  and and_7 (and_5_out[2], ~in_3, in_2[2]);  // AND_Gate
  and and_8 (and_5_out[3], ~in_3, in_2[3]);  // AND_Gate
  assign out_4 = and_1_out | and_5_out;  // OR_Gate or_1, 4 bits wide
endmodule

// COMP
module COMPARADOR (
  input  [4:0] in_1,
  input  [4:0] CHUTE,
  output [2:0] out_3
);

  wire _0_2_out, _0_out, _1_2_out, _1_out, _2_2_out, _2_out, _3_2_out, _3_3_out, _3_out, _4_out;

  xnor _0 (_0_out, in_1[0], CHUTE[0]);
  xnor _1 (_1_out, in_1[1], CHUTE[1]);
  xnor _2 (_2_out, in_1[2], CHUTE[2]);
  xnor _3 (_3_out, in_1[3], CHUTE[3]);
  xnor _4 (_4_out, in_1[4], CHUTE[4]);
  and IGUAL (out_3[1], _0_out, _1_out, _2_out, _3_out);
  and _0_2 (_0_2_out, CHUTE[0], _1_out, _2_out, _3_out, ~in_1[0], _4_out);  // AND_Gate
  and _1_2 (_1_2_out, CHUTE[1], ~in_1[1], _4_out, _2_out, _3_out);  // AND_Gate
  and _2_2 (_2_2_out, CHUTE[2], ~in_1[2], _3_out, _4_out);  // AND_Gate
  and _3_2 (_3_2_out, CHUTE[3], ~in_1[3], _4_out);  // AND_Gate
  and _3_3 (_3_3_out, CHUTE[4], ~in_1[4]);  // AND_Gate
  or MAIOR (out_3[2], _0_2_out, _1_2_out, _3_3_out, _2_2_out, _3_2_out);
  nor MENOR (out_3[0], out_3[1], out_3[2]);
endmodule

module SUM (
  input  in_1,
  input  in_2,
  input  in_3,
  output SUM,
  output CARRY
);

  wire AND_2_out, AND_3_out, AND_out, xor_1_out;

  xor xor_1 (xor_1_out, in_1, in_2);
  xor xor_2 (SUM, xor_1_out, in_3);
  and AND (AND_out, in_1, in_2);
  and AND_2 (AND_2_out, in_1, in_3);
  and AND_3 (AND_3_out, in_2, in_3);
  or or_1 (CARRY, AND_out, AND_2_out, AND_3_out);
endmodule

// SOMA
module SOMADOR (
  input  [4:0] in_1,
  input  [4:0] in_2,
  output [4:0] out_3
);

  wire sum_1_carry, sum_2_carry, sum_3_carry;

  SUM sum_1 (.in_1(in_1[4]), .in_2(in_1[0]), .in_3(in_2[0]), .SUM(out_3[0]), .CARRY(sum_1_carry));
  SUM sum_2 (.in_1(sum_1_carry), .in_2(in_1[1]), .in_3(in_2[1]), .SUM(out_3[1]), .CARRY(sum_2_carry));
  SUM sum_3 (.in_1(sum_2_carry), .in_2(in_1[2]), .in_3(in_2[2]), .SUM(out_3[2]), .CARRY(sum_3_carry));
  SUM sum_4 (.in_1(sum_3_carry), .in_2(in_1[3]), .in_3(in_2[3]), .SUM(out_3[3]), .CARRY(out_3[4]));

  assign in_2[4] = in_1[4];
  // also tied to GND on the sheet: in_1[4]
endmodule

module \VARIÁVEL  (
  input  [3:0] in_1,
  input  CLK,
  input  CLEAR,
  input  ENABLE,
  output [4:0] out_5,
  output [3:0] out_6
);

  D_Flip_Flop #(.trigger("falling")) d_ff_1 (
    .clk(CLK), .D(in_1[3]), .Q(out_5[3]), .en(ENABLE), .reset(CLEAR));  // open: Qn, preset
  D_Flip_Flop #(.trigger("falling")) d_ff_2 (
    .clk(CLK), .D(in_1[2]), .Q(out_5[2]), .en(ENABLE), .reset(CLEAR));  // open: Qn, preset
  D_Flip_Flop #(.trigger("falling")) d_ff_3 (
    .clk(CLK), .D(in_1[1]), .Q(out_5[1]), .en(ENABLE), .reset(CLEAR));  // open: Qn, preset
  D_Flip_Flop #(.trigger("falling")) d_ff_4 (
    .clk(CLK), .D(in_1[0]), .Q(out_5[0]), .en(ENABLE), .reset(CLEAR));  // open: Qn, preset
  Hex_Digit_Display hex_digit_display_1 (.value(out_5[3:0]));  // open: dp

  assign out_5[4] = 1'b0;
  assign out_6 = out_5[3:0];
endmodule

module passarChute (
  input  ENABLE,
  input  CLK,
  input  CLEAR,
  input  [4:0] in_4,
  input  [4:0] in_5,
  output [4:0] out_6,
  output [4:0] out_7
);

  wire [3:0] and_1_out, and_5_out;

  and and_1 (and_1_out[0], in_4[0], CLK);
  and and_2 (and_1_out[1], in_4[1], CLK);
  and and_3 (and_1_out[2], in_4[2], CLK);
  and and_4 (and_1_out[3], in_4[3], CLK);
  and and_5 (and_5_out[0], CLK, in_5[0]);
  and and_6 (and_5_out[1], CLK, in_5[1]);
  and and_7 (and_5_out[2], CLK, in_5[2]);
  and and_8 (and_5_out[3], CLK, in_5[3]);
  \VARIÁVEL  \variável_1  (.in_1(and_1_out), .CLK(CLK), .CLEAR(CLEAR), .ENABLE(ENABLE), .out_5(out_6));  // open: out_6
  \VARIÁVEL  \variável_2  (.in_1(and_5_out), .CLK(CLK), .CLEAR(CLEAR), .ENABLE(ENABLE), .out_5(out_7));  // open: out_6

  assign in_5[4] = in_4[4];
  // also tied to GND on the sheet: in_4[4]
endmodule

module \BOTÃO  (
  input  PROXIMO,
  output CLK,
  output Q0,
  output Q1
);

  wire not_1_out;

  not not_1 (not_1_out, Q0);
  D_Flip_Flop d_ff_1 (.clk(PROXIMO), .D(not_1_out), .Q(Q0));  // open: Qn, preset, en, reset
  not not_2 (Q1, Q0);

  assign CLK = PROXIMO;
endmodule

module FLIPFLOPD_DESCIDA (
  input  D,
  input  CLK,
  input  ENABLE,
  input  CLEAR,
  output Q
);

  wire and_1_out, and_2_out, and_3_out, nor_2_out, not_1_out, not_2_out, not_3_out, not_4_out, not_5_out;

  not not_1 (not_1_out, CLK);
  not not_2 (not_2_out, not_3_out);
  not not_3 (not_3_out, not_4_out);
  not not_4 (not_4_out, not_1_out);
  not not_5 (not_5_out, D);
  and and_1 (and_1_out, not_1_out, ENABLE, not_2_out);
  and and_2 (and_2_out, not_5_out, and_1_out);
  nor nor_1 (Q, and_2_out, CLEAR, nor_2_out);
  nor nor_2 (nor_2_out, Q, and_3_out);
  and and_3 (and_3_out, and_1_out, D);
endmodule
