// Logisim project PROJETO.2 - CD.circ as structural Verilog: 36 circuits, main circuit main
module main (
  input  [3:0] in_1,
  input  [3:0] in_2
);

  wire aux_3_1_out_9, aux_3_1_out_10, aux_3_1_out_11, aux_3_1_out_12, button_1_out, CHUTE_out, core_1__1,
       core_1__2, core_1_ligado, core_1_negx, core_1_negy, core_1_out_9, core_1_out_12, core_1_out_13,
       core_1_out_14, core_1_x, core_1_y, \CRÔNOMETRO_2_zer , \CRÔNOMETRO_zer , displayfinal_1_out_2,
       displayfinal_2_out_2, DMA_2_out, DMA_out, DSA_2_out, DSA_out, LIG_out, not_1_out, PROXIMO_out,
       UMA_2_out, UMA_out, USA_2_out, USA_out, ZERA_out;
  wire [3:0] core_1_display_a___x, core_1_display_a___y, core_1_display_b___x, core_1_display_b___y,
       core_1_pontoa, core_1_pontob, \CRÔNOMETRO_2_c0 , \CRÔNOMETRO_2_c1 , \CRÔNOMETRO_2_c2 ,
       \CRÔNOMETRO_2_c3 , \CRÔNOMETRO_c0 , \CRÔNOMETRO_c1 , \CRÔNOMETRO_c2 , \CRÔNOMETRO_c3 ,
       display_0_f_1_inferior, display_0_f_1_superior, display_0_f_2_inferior, display_0_f_2_superior,
       display_0_f_3_inferior, display_0_f_3_superior, display_0_f_4_inferior, display_0_f_4_superior,
       display_0_f_5_inferior, display_0_f_5_superior, display_0_f_6_inferior, display_0_f_6_superior,
       display_0_f_7_inferior, display_0_f_7_superior, display_0_f_8_inferior, display_0_f_8_superior,
       displayfinal_1_out_3, displayfinal_1_out_4, displayfinal_2_out_3, displayfinal_2_out_4;

  Button DMA (.out(DMA_out));
  Button UMA (.out(UMA_out));
  Button DSA (.out(DSA_out));
  cronometro \CRÔNOMETRO  (
    .ENABLE(LIG_out), .CLEAR(ZERA_out), .CONF(button_1_out), .C3(\CRÔNOMETRO_c3 ), .C2(\CRÔNOMETRO_c2 ),
    .C1(\CRÔNOMETRO_c1 ), .C0(\CRÔNOMETRO_c0 ), .in_3(aux_3_1_out_12), .in_1(aux_3_1_out_11),
    .in_2(aux_3_1_out_10), .in_4(aux_3_1_out_9), .Zer(\CRÔNOMETRO_zer ), .in_8(not_1_out));  // open: lig, Conf_2
  Button USA (.out(USA_out));
  aux_3 aux_3_1 (
    .in_1(USA_out), .in_2(USA_2_out), .in_3(DSA_out), .in_4(DSA_2_out), .in_5(UMA_out), .in_6(UMA_2_out),
    .in_7(DMA_out), .in_8(DMA_2_out), .out_9(aux_3_1_out_9), .out_10(aux_3_1_out_10),
    .out_11(aux_3_1_out_11), .out_12(aux_3_1_out_12));
  not not_1 (not_1_out, core_1_out_9);
  _7_Segment_Display u_7_segment_display_1 (.g(displayfinal_1_out_2));  // open: f, a, b, e, d, c, dp
  Button UMA_2 (.out(UMA_2_out));
  Button DMA_2 (.out(DMA_2_out));
  cronometro \CRÔNOMETRO_2  (
    .ENABLE(LIG_out), .CLEAR(ZERA_out), .CONF(button_1_out), .C3(\CRÔNOMETRO_2_c3 ), .C2(\CRÔNOMETRO_2_c2 ),
    .C1(\CRÔNOMETRO_2_c1 ), .C0(\CRÔNOMETRO_2_c0 ), .in_3(aux_3_1_out_12), .in_1(aux_3_1_out_11),
    .in_2(aux_3_1_out_10), .in_4(aux_3_1_out_9), .Zer(\CRÔNOMETRO_2_zer ), .in_8(core_1_out_9));  // open: lig, Conf_2
  _7_Segment_Display u_7_segment_display_2 (
    .g(display_0_f_2_superior[3]), .f(display_0_f_2_superior[2]), .a(display_0_f_2_superior[1]),
    .b(display_0_f_2_superior[0]), .e(display_0_f_2_inferior[3]), .d(display_0_f_2_inferior[2]),
    .c(display_0_f_2_inferior[1]), .dp(display_0_f_2_inferior[0]));
  LED _1 (.in(core_1__1));
  displayFinal displayfinal_1 (
    .in_1(in_1), .out_2(displayfinal_1_out_2), .out_3(displayfinal_1_out_3), .out_4(displayfinal_1_out_4));
  _7_Segment_Display u_7_segment_display_3 (
    .g(displayfinal_1_out_4[3]), .f(displayfinal_1_out_4[2]), .a(displayfinal_1_out_4[1]),
    .b(displayfinal_1_out_4[0]), .e(displayfinal_1_out_3[3]), .d(displayfinal_1_out_3[2]),
    .c(displayfinal_1_out_3[1]), .dp(displayfinal_1_out_3[0]));
  Button DSA_2 (.out(DSA_2_out));
  Button USA_2 (.out(USA_2_out));
  display_0_f display_0_f_1 (
    .in_1(\CRÔNOMETRO_2_c2 ), .SUPERIOR(display_0_f_1_superior), .INFERIOR(display_0_f_1_inferior));
  display_0_f display_0_f_2 (
    .in_1(\CRÔNOMETRO_2_c3 ), .SUPERIOR(display_0_f_2_superior), .INFERIOR(display_0_f_2_inferior));
  _7_Segment_Display u_7_segment_display_4 (
    .g(display_0_f_1_superior[3]), .f(display_0_f_1_superior[2]), .a(display_0_f_1_superior[1]),
    .b(display_0_f_1_superior[0]), .e(display_0_f_1_inferior[3]), .d(display_0_f_1_inferior[2]),
    .c(display_0_f_1_inferior[1]), .dp(display_0_f_1_inferior[0]));
  display_0_f display_0_f_3 (
    .in_1(\CRÔNOMETRO_2_c1 ), .SUPERIOR(display_0_f_3_superior), .INFERIOR(display_0_f_3_inferior));
  _7_Segment_Display u_7_segment_display_5 (
    .g(display_0_f_3_superior[3]), .f(display_0_f_3_superior[2]), .a(display_0_f_3_superior[1]),
    .b(display_0_f_3_superior[0]), .e(display_0_f_3_inferior[3]), .d(display_0_f_3_inferior[2]),
    .c(display_0_f_3_inferior[1]), .dp(display_0_f_3_inferior[0]));
  LED led_1 (.in(1'b1));
  LED led_2 (.in(1'b1));
  Button PROXIMO (.out(PROXIMO_out));
  Button CHUTE (.out(CHUTE_out));
  Button ZERA (.out(ZERA_out));
  Button LIG (.out(LIG_out));
  LED X (.in(core_1_x));
  _7_Segment_Display u_7_segment_display_6 (.g(core_1_negx));  // open: f, a, b, e, d, c, dp
  display_0_f display_0_f_4 (
    .in_1(\CRÔNOMETRO_2_c0 ), .SUPERIOR(display_0_f_4_superior), .INFERIOR(display_0_f_4_inferior));
  _7_Segment_Display u_7_segment_display_7 (
    .g(display_0_f_4_superior[3]), .f(display_0_f_4_superior[2]), .a(display_0_f_4_superior[1]),
    .b(display_0_f_4_superior[0]), .e(display_0_f_4_inferior[3]), .d(display_0_f_4_inferior[2]),
    .c(display_0_f_4_inferior[1]), .dp(display_0_f_4_inferior[0]));
  Button button_1 (.out(button_1_out));
  Hex_Digit_Display hex_digit_display_1 (.value(core_1_pontoa));  // open: dp
  LED LIGADO (.in(core_1_ligado));
  _7_Segment_Display u_7_segment_display_8 (
    .g(core_1_display_b___x[3]), .f(core_1_display_b___x[2]), .a(core_1_display_b___x[1]),
    .b(core_1_display_b___x[0]), .e(core_1_display_a___x[3]), .d(core_1_display_a___x[2]),
    .c(core_1_display_a___x[1]), .dp(core_1_display_a___x[0]));
  display_0_f display_0_f_5 (
    .in_1(\CRÔNOMETRO_c3 ), .SUPERIOR(display_0_f_5_superior), .INFERIOR(display_0_f_5_inferior));
  _7_Segment_Display u_7_segment_display_9 (
    .g(display_0_f_5_superior[3]), .f(display_0_f_5_superior[2]), .a(display_0_f_5_superior[1]),
    .b(display_0_f_5_superior[0]), .e(display_0_f_5_inferior[3]), .d(display_0_f_5_inferior[2]),
    .c(display_0_f_5_inferior[1]), .dp(display_0_f_5_inferior[0]));
  Hex_Digit_Display hex_digit_display_2 (.value(core_1_pontob));  // open: dp
  display_0_f display_0_f_6 (
    .in_1(\CRÔNOMETRO_c2 ), .SUPERIOR(display_0_f_6_superior), .INFERIOR(display_0_f_6_inferior));
  _7_Segment_Display u_7_segment_display_10 (
    .g(display_0_f_6_superior[3]), .f(display_0_f_6_superior[2]), .a(display_0_f_6_superior[1]),
    .b(display_0_f_6_superior[0]), .e(display_0_f_6_inferior[3]), .d(display_0_f_6_inferior[2]),
    .c(display_0_f_6_inferior[1]), .dp(display_0_f_6_inferior[0]));
  LED led_3 (.in(1'b1));
  LED led_4 (.in(1'b1));
  LED led_5 (.in(core_1_out_12));
  CORE core_1 (
    .PROXIMO(PROXIMO_out), .CHUTE(CHUTE_out), .CLEAR(ZERA_out), .ENABLE(LIG_out), .out_9(core_1_out_9),
    .pontoA(core_1_pontoa), .pontoB(core_1_pontob), .RESET(\CRÔNOMETRO_2_zer ), .PRESET(\CRÔNOMETRO_zer ),
    .ENTRADA(in_1), .ENTRADA_2(in_2), .ligado(core_1_ligado), ._1(core_1__1), ._2(core_1__2), .X(core_1_x),
    .Y(core_1_y), .negX(core_1_negx), .DISPLAY_A___x(core_1_display_a___x),
    .DISPLAY_B___x(core_1_display_b___x), .negY(core_1_negy), .DISPLAY_A___Y(core_1_display_a___y),
    .DISPLAY_B___Y(core_1_display_b___y), .out_12(core_1_out_12), .out_13(core_1_out_13),
    .out_14(core_1_out_14));
  LED Y (.in(core_1_y));
  _7_Segment_Display u_7_segment_display_11 (
    .g(core_1_display_b___y[3]), .f(core_1_display_b___y[2]), .a(core_1_display_b___y[1]),
    .b(core_1_display_b___y[0]), .e(core_1_display_a___y[3]), .d(core_1_display_a___y[2]),
    .c(core_1_display_a___y[1]), .dp(core_1_display_a___y[0]));
  _7_Segment_Display u_7_segment_display_12 (.g(core_1_negy));  // open: f, a, b, e, d, c, dp
  display_0_f display_0_f_7 (
    .in_1(\CRÔNOMETRO_c1 ), .SUPERIOR(display_0_f_7_superior), .INFERIOR(display_0_f_7_inferior));
  _7_Segment_Display u_7_segment_display_13 (
    .g(display_0_f_8_superior[3]), .f(display_0_f_8_superior[2]), .a(display_0_f_8_superior[1]),
    .b(display_0_f_8_superior[0]), .e(display_0_f_8_inferior[3]), .d(display_0_f_8_inferior[2]),
    .c(display_0_f_8_inferior[1]), .dp(display_0_f_8_inferior[0]));
  _7_Segment_Display u_7_segment_display_14 (
    .g(display_0_f_7_superior[3]), .f(display_0_f_7_superior[2]), .a(display_0_f_7_superior[1]),
    .b(display_0_f_7_superior[0]), .e(display_0_f_7_inferior[3]), .d(display_0_f_7_inferior[2]),
    .c(display_0_f_7_inferior[1]), .dp(display_0_f_7_inferior[0]));
  LED led_6 (.in(core_1_out_14));
  LED led_7 (.in(core_1_out_13));
  display_0_f display_0_f_8 (
    .in_1(\CRÔNOMETRO_c0 ), .SUPERIOR(display_0_f_8_superior), .INFERIOR(display_0_f_8_inferior));
  _7_Segment_Display u_7_segment_display_15 (.g(displayfinal_2_out_2));  // open: f, a, b, e, d, c, dp
  LED _2 (.in(core_1__2));
  displayFinal displayfinal_2 (
    .in_1(in_2), .out_2(displayfinal_2_out_2), .out_3(displayfinal_2_out_3), .out_4(displayfinal_2_out_4));
  _7_Segment_Display u_7_segment_display_16 (
    .g(displayfinal_2_out_4[3]), .f(displayfinal_2_out_4[2]), .a(displayfinal_2_out_4[1]),
    .b(displayfinal_2_out_4[0]), .e(displayfinal_2_out_3[3]), .d(displayfinal_2_out_3[2]),
    .c(displayfinal_2_out_3[1]), .dp(displayfinal_2_out_3[0]));
endmodule

// 5-0
module contadorDezenal (
  input  CLKBTN,
  input  CONF,
  input  CLK,
  input  CLEAR,
  input  ENABLE,
  output [3:0] out_6,
  output out_7,
  output out_8
);

  wire and_1_out, and_2_out, decrementardezena_1_q0, decrementardezena_1_q1, decrementardezena_1_q2,
       decrementardezena_1_q3, or_1_out;

  and and_1 (and_1_out, CLKBTN, CONF);
  and and_2 (and_2_out, CLK, ~CONF);  // AND_Gate
  or or_1 (or_1_out, and_1_out, and_2_out);
  D_Flip_Flop d_ff_1 (
    .clk(or_1_out), .D(decrementardezena_1_q0), .Q(out_6[3]), .en(ENABLE), .reset(CLEAR));  // open: Qn, preset
  D_Flip_Flop d_ff_2 (
    .clk(or_1_out), .D(decrementardezena_1_q1), .Q(out_6[2]), .en(ENABLE), .reset(CLEAR));  // open: Qn, preset
  decrementarDezena decrementardezena_1 (
    .D0(out_6[3]), .D1(out_6[2]), .D2(out_6[1]), .D3(out_6[0]), .Q0(decrementardezena_1_q0),
    .Q1(decrementardezena_1_q1), .Q2(decrementardezena_1_q2), .Q3(decrementardezena_1_q3), .SS(out_8),
    .zz(out_7));
  D_Flip_Flop d_ff_3 (
    .clk(or_1_out), .D(decrementardezena_1_q2), .Q(out_6[1]), .en(ENABLE), .reset(CLEAR));  // open: Qn, preset
  Hex_Digit_Display hex_digit_display_1 (.value(out_6));  // open: dp
  D_Flip_Flop d_ff_4 (
    .clk(or_1_out), .D(decrementardezena_1_q3), .Q(out_6[0]), .en(ENABLE), .reset(CLEAR));  // open: Qn, preset
endmodule

// 9-0
module contadorUnidade (
  input  CLKBTN,
  input  CONF,
  input  CLK,
  input  CLEAR,
  input  ENABLE,
  output [3:0] out_6,
  output out_7,
  output out_8
);

  wire and_1_out, and_2_out, decrementarunidade_1_q0, decrementarunidade_1_q1, decrementarunidade_1_q2,
       decrementarunidade_1_q3, or_1_out;

  and and_1 (and_1_out, CLKBTN, CONF);
  and and_2 (and_2_out, CLK, ~CONF);  // AND_Gate
  or or_1 (or_1_out, and_1_out, and_2_out);
  D_Flip_Flop d_ff_1 (
    .clk(or_1_out), .D(decrementarunidade_1_q0), .Q(out_6[3]), .en(ENABLE), .reset(CLEAR));  // open: Qn, preset
  D_Flip_Flop d_ff_2 (
    .clk(or_1_out), .D(decrementarunidade_1_q1), .Q(out_6[2]), .en(ENABLE), .reset(CLEAR));  // open: Qn, preset
  decrementarUnidade decrementarunidade_1 (
    .D0(out_6[3]), .D1(out_6[2]), .D2(out_6[1]), .D3(out_6[0]), .Q0(decrementarunidade_1_q0),
    .Q1(decrementarunidade_1_q1), .Q2(decrementarunidade_1_q2), .Q3(decrementarunidade_1_q3), .SS(out_8),
    .zz(out_7));
  D_Flip_Flop d_ff_3 (
    .clk(or_1_out), .D(decrementarunidade_1_q2), .Q(out_6[1]), .en(ENABLE), .reset(CLEAR));  // open: Qn, preset
  Hex_Digit_Display hex_digit_display_1 (.value(out_6));  // open: dp
  D_Flip_Flop d_ff_4 (
    .clk(or_1_out), .D(decrementarunidade_1_q3), .Q(out_6[0]), .en(ENABLE), .reset(CLEAR));  // open: Qn, preset
endmodule

module display_0_f (
  input  [3:0] in_1,
  output [3:0] SUPERIOR,
  output [3:0] INFERIOR
);

  wire and_1_out, and_2_out, and_3_out, and_4_out, and_5_out, and_6_out, and_7_out, and_8_out, and_9_out,
       and_10_out, and_11_out, and_12_out, and_13_out, and_14_out, and_15_out, and_16_out, and_17_out,
       and_18_out, and_19_out, and_20_out, and_22_out, and_23_out, and_24_out, nand_1_out, nor_1_out,
       nor_2_out, nor_3_out, nor_4_out, nor_5_out, or_1_out, or_2_out, or_3_out, or_4_out, or_5_out,
       or_6_out, or_7_out, or_8_out, xor_1_out, xor_2_out, xor_3_out;

  or or_1 (or_1_out, in_1[3], ~in_1[2]);  // OR_Gate
  or or_2 (or_2_out, ~in_1[3], in_1[2]);  // OR_Gate
  and and_1 (and_1_out, ~in_1[3], in_1[2], in_1[0]);  // AND_Gate
  and and_2 (and_2_out, in_1[3], ~in_1[2], ~in_1[1]);  // AND_Gate
  xor xor_1 (xor_1_out, in_1[3], in_1[1]);
  nand nand_1 (nand_1_out, in_1[3], in_1[0]);
  nor nor_1 (nor_1_out, in_1[3], in_1[1], in_1[0]);
  and and_3 (and_3_out, ~in_1[1], in_1[0]);  // AND_Gate
  xor xor_2 (xor_2_out, in_1[3], in_1[2]);
  and and_4 (and_4_out, in_1[1], in_1[0]);
  nor nor_2 (nor_2_out, in_1[1], in_1[0]);
  and and_5 (and_5_out, in_1[2], in_1[0]);
  nor nor_3 (nor_3_out, in_1[2], in_1[0]);
  nor nor_4 (nor_4_out, in_1[3], in_1[2]);
  xor xor_3 (xor_3_out, in_1[2], in_1[0]);
  or or_3 (or_3_out, ~in_1[2], in_1[1]);  // OR_Gate
  or or_4 (or_4_out, in_1[2], in_1[1]);
  and and_6 (and_6_out, in_1[3], in_1[1]);
  and and_7 (and_7_out, in_1[3], ~in_1[2]);  // AND_Gate
  nor nor_5 (nor_5_out, in_1[1], in_1[0]);
  and and_8 (and_8_out, in_1[2], ~in_1[0]);  // AND_Gate
  and and_9 (and_9_out, ~in_1[1], in_1[2], ~in_1[3]);  // AND_Gate
  and and_10 (and_10_out, in_1[1], ~in_1[0]);  // AND_Gate
  and and_11 (and_11_out, in_1[3], ~in_1[2]);  // AND_Gate
  and and_12 (and_12_out, in_1[3], in_1[0]);
  and and_13 (and_13_out, ~in_1[3], in_1[2], ~in_1[1]);  // AND_Gate
  and and_14 (and_14_out, ~in_1[2], in_1[1], in_1[0]);  // AND_Gate
  or or_5 (or_5_out, in_1[2], in_1[1]);
  and and_15 (and_15_out, or_1_out, ~in_1[0]);  // AND_Gate
  and and_16 (and_16_out, in_1[1], or_2_out);
  and and_17 (and_17_out, xor_1_out, in_1[0]);
  and and_18 (and_18_out, nand_1_out, ~in_1[2]);  // AND_Gate
  or or_6 (or_6_out, and_4_out, nor_2_out);
  or or_7 (or_7_out, and_5_out, in_1[3], nor_3_out);
  or or_8 (or_8_out, nor_4_out, xor_3_out);
  and and_19 (and_19_out, ~in_1[0], or_3_out);  // AND_Gate
  or E (INFERIOR[3], and_19_out, and_20_out);
  and and_20 (and_20_out, or_4_out, in_1[3]);
  or F (SUPERIOR[2], and_6_out, and_7_out, nor_5_out, and_8_out, and_9_out);
  or G (SUPERIOR[3], and_10_out, and_11_out, and_12_out, and_13_out, and_14_out);
  and and_21 (INFERIOR[0], in_1[3], or_5_out);
  or A (SUPERIOR[1], and_15_out, and_16_out, and_1_out, and_2_out);
  or B (SUPERIOR[0], and_17_out, and_18_out, nor_1_out);
  or C (INFERIOR[1], and_3_out, xor_2_out, and_22_out);
  and and_22 (and_22_out, or_6_out, ~in_1[3]);  // AND_Gate
  and and_23 (and_23_out, or_7_out, ~in_1[1]);  // AND_Gate
  or D (INFERIOR[2], and_23_out, and_24_out);
  and and_24 (and_24_out, in_1[1], or_8_out);
endmodule

module cronometro (
  input  in_1,
  input  in_2,
  input  in_3,
  input  in_4,
  input  ENABLE,
  input  CLEAR,
  input  CONF,
  input  in_8,
  output [3:0] C3,
  output [3:0] C2,
  output [3:0] C1,
  output [3:0] C0,
  output Zer,
  output lig,
  output Conf_2
);

  wire and_1_out, clock_1_out, contadordezenal_1_out_7, contadordezenal_2_out_7, contadordezenal_2_out_8,
       contadorunidade_1_out_7, contadorunidade_1_out_8, contadorunidade_2_out_7, contadorunidade_2_out_8;

  botao botao_1 (.PROXIMO(ENABLE), .Q0(lig));  // open: CLK, Q1
  Clock clock_1 (.out(clock_1_out));
  Hex_Digit_Display hex_digit_display_1 (.value(C3));  // open: dp
  and and_1 (and_1_out, lig, ~Zer, clock_1_out, in_8);  // AND_Gate
  botao botao_2 (.PROXIMO(CONF), .Q0(Conf_2));  // open: CLK, Q1
  Hex_Digit_Display hex_digit_display_2 (.value(C2));  // open: dp
  contadorDezenal contadordezenal_1 (
    .CLK(contadorunidade_1_out_8), .CLEAR(CLEAR), .ENABLE(lig), .out_6(C3), .out_7(contadordezenal_1_out_7),
    .CLKBTN(in_3), .CONF(Conf_2));  // open: out_8
  Hex_Digit_Display hex_digit_display_3 (.value(C1));  // open: dp
  contadorDezenal contadordezenal_2 (
    .out_8(contadordezenal_2_out_8), .CLK(contadorunidade_2_out_8), .CLEAR(CLEAR), .ENABLE(lig), .out_6(C1),
    .out_7(contadordezenal_2_out_7), .CLKBTN(in_2), .CONF(Conf_2));
  contadorUnidade contadorunidade_1 (
    .out_8(contadorunidade_1_out_8), .CLK(contadordezenal_2_out_8), .CLEAR(CLEAR), .ENABLE(lig), .out_6(C2),
    .out_7(contadorunidade_1_out_7), .CLKBTN(in_1), .CONF(Conf_2));
  Hex_Digit_Display hex_digit_display_4 (.value(C0));  // open: dp
  contadorUnidade contadorunidade_2 (
    .out_8(contadorunidade_2_out_8), .CLK(and_1_out), .CLEAR(CLEAR), .ENABLE(lig), .out_6(C0),
    .out_7(contadorunidade_2_out_7), .CLKBTN(in_4), .CONF(Conf_2));
  and and_2 (Zer, contadorunidade_2_out_7, contadordezenal_2_out_7, contadorunidade_1_out_7, contadordezenal_1_out_7);
endmodule

module CORE (
  input  PROXIMO,
  input  CHUTE,
  input  RESET,
  input  PRESET,
  input  CLEAR,
  input  ENABLE,
  input  [3:0] ENTRADA,
  input  [3:0] ENTRADA_2,
  output out_9,
  output [3:0] pontoA,
  output [3:0] pontoB,
  output out_12,
  output out_13,
  output out_14,
  output ligado,
  output _1,
  output _2,
  output X,
  output Y,
  output negX,
  output [3:0] DISPLAY_A___x,
  output [3:0] DISPLAY_B___x,
  output negY,
  output [3:0] DISPLAY_A___Y,
  output [3:0] DISPLAY_B___Y
);

  wire and_1_out, and_2_out, botao_1_q0, core_2_1_comp1, core_2_1_comp2, verificador_1__0, verificador_1__1,
       verificador_1__2, verificador_1__3;
  wire [3:0] core_1_1_saida, core_1_2_saida, multiplexjogadores_1_out_4;

  botao botao_1 (.PROXIMO(ENABLE), .Q0(botao_1_q0));  // open: CLK, Q1
  and and_1 (and_1_out, ~and_2_out, botao_1_q0);  // AND_Gate
  multiplexJogadores multiplexjogadores_1 (
    .in_1(ENTRADA), .in_2(ENTRADA_2), .in_3(out_9), .out_4(multiplexjogadores_1_out_4));
  verificador verificador_1 (
    .ENABLE(and_1_out), .CLEAR(CLEAR), .PROX(PROXIMO), ._0(verificador_1__0), ._1(verificador_1__1),
    ._2(verificador_1__2), ._3(verificador_1__3));
  coreLeds coreleds_1 (
    .ENABLE(and_1_out), .JOGADOR(out_9), ._1(verificador_1__0), ._2(verificador_1__1), .ligado(ligado),
    ._1_2(_1), ._2_2(_2), .X(X), .Y(Y));
  core_1 core_1_1 (
    .CHUTE(CHUTE), ._1(verificador_1__0), .ENABLE(and_1_out), .in_6(multiplexjogadores_1_out_4),
    ._2(verificador_1__2), .CLEAR(CLEAR), .neg(negX), .DISPLAY_A(DISPLAY_A___x), .DISPLAY_B(DISPLAY_B___x),
    .SAIDA(core_1_1_saida));
  core_1 core_1_2 (
    .CHUTE(CHUTE), ._1(verificador_1__1), .ENABLE(and_1_out), .in_6(multiplexjogadores_1_out_4),
    ._2(verificador_1__2), .CLEAR(CLEAR), .neg(negY), .DISPLAY_A(DISPLAY_A___Y), .DISPLAY_B(DISPLAY_B___Y),
    .SAIDA(core_1_2_saida));
  core_2 core_2_1 (
    .enable(and_1_out), ._2(verificador_1__2), .in_7(core_1_1_saida), .in_8(core_1_2_saida), .clear(CLEAR),
    ._3(verificador_1__3), .valor1(4'b0001), .comp1(core_2_1_comp1), .valor2(4'b0001),
    .comp2(core_2_1_comp2), .menor(out_12), .igual(out_13), .maior(out_14));
  core_3 core_3_1 (
    ._3(verificador_1__3), .jogador(out_9), .comp1(core_2_1_comp1), .comp2(core_2_1_comp2),
    ._2(verificador_1__2), .clear(CLEAR), .pontoA(pontoA), .pontoB(pontoB), .RESET(RESET), .PRESET(PRESET));
  and and_2 (and_2_out, RESET, PRESET);

  // Notes on the sheet:
  //   cronometro zerado para o jogador
endmodule

module core_1 (
  input  CHUTE,
  input  _2,
  input  CLEAR,
  input  _1,
  input  ENABLE,
  input  [3:0] in_6,
  output [3:0] SAIDA,
  output neg,
  output [3:0] DISPLAY_A,
  output [3:0] DISPLAY_B
);

  wire and_1_out, or_1_out;

  and and_1 (and_1_out, CHUTE, _1);
  displayFinal displayfinal_1 (.in_1(SAIDA), .out_2(neg), .out_3(DISPLAY_A), .out_4(DISPLAY_B));
  varialvel Y (.in_1(in_6), .CLK(and_1_out), .CLEAR(or_1_out), .ENABLE(ENABLE), .out_5(SAIDA));
  or or_1 (or_1_out, _2, CLEAR);
endmodule

// COMP
module comparadorQuatroBits (
  input  [3:0] CHUTE,
  input  NEG,
  input  [3:0] in_3,
  output [2:0] out_4
);

  wire _0_2_out, _0_out, _1_2_out, _1_out, _2_2_out, _2_out, _3_2_out, _3_out, MAIOR_out, MENOR_out;

  xnor _0 (_0_out, in_3[0], CHUTE[0]);
  xnor _1 (_1_out, in_3[1], CHUTE[1]);
  xnor _2 (_2_out, in_3[2], CHUTE[2]);
  xnor _3 (_3_out, in_3[3], CHUTE[3]);
  and IGUAL (out_4[1], _0_out, _1_out, _2_out, _3_out);
  and _0_2 (_0_2_out, CHUTE[0], _1_out, _2_out, _3_out, ~in_3[0]);  // AND_Gate
  and _1_2 (_1_2_out, CHUTE[1], ~in_3[1], _2_out, _3_out);  // AND_Gate
  and _2_2 (_2_2_out, CHUTE[2], ~in_3[2], _3_out);  // AND_Gate
  and _3_2 (_3_2_out, CHUTE[3], ~in_3[3]);  // AND_Gate
  or MAIOR (MAIOR_out, _0_2_out, _1_2_out, _2_2_out, _3_2_out);
  nor MENOR (MENOR_out, out_4[1], MAIOR_out);
  xor xor_1 (out_4[0], NEG, MENOR_out);
  xor xor_2 (out_4[2], NEG, MAIOR_out);
endmodule

module soma (
  input  in_1,
  input  in_2,
  input  in_3,
  output SUM,
  output CARRY
);

  wire AND_2_out, AND_3_out, AND_out, xor_1_out;

  xor xor_1 (xor_1_out, in_1, in_2);
  xor xor_2 (SUM, xor_1_out, in_3);
  and AND (AND_out, in_1, in_2);
  and AND_2 (AND_2_out, in_1, in_3);
  and AND_3 (AND_3_out, in_2, in_3);
  or or_1 (CARRY, AND_out, AND_2_out, AND_3_out);
endmodule

// SOMA
module somador (
  input  [3:0] in_1,
  input  [3:0] in_2,
  output [4:0] out_3,
  output out_4
);

  wire and_1_out, and_2_out, soma_1_carry, soma_2_carry, soma_3_carry;
  wire [2:0] comparadorquatrobits_1_out_4, comparadorquatrobits_2_out_4;
  wire [3:0] not_1_out, not_2_out, subtrair_1_q3, subtrair_2_q0;

  SUBTRAIR subtrair_1 (
    .D0(in_1[3]), .D1(in_1[2]), .D2(in_1[1]), .D3(in_1[0]), .Q0(subtrair_1_q3[3]), .Q1(subtrair_1_q3[2]),
    .Q2(subtrair_1_q3[1]), .Q3(subtrair_1_q3[0]));
  assign not_1_out = ~subtrair_1_q3;  // NOT_Gate not_1, 4 bits wide
  assign not_2_out = ~in_1;  // NOT_Gate not_2, 4 bits wide
  SUBTRAIR subtrair_2 (
    .D0(in_2[3]), .D1(in_2[2]), .D2(in_2[1]), .D3(in_2[0]), .Q0(subtrair_2_q0[0]), .Q1(subtrair_2_q0[1]),
    .Q2(subtrair_2_q0[2]), .Q3(subtrair_2_q0[3]));
  comparadorQuatroBits comparadorquatrobits_1 (
    .CHUTE(not_1_out), .in_3(in_2), .NEG(1'b0), .out_4(comparadorquatrobits_1_out_4));
  comparadorQuatroBits comparadorquatrobits_2 (
    .CHUTE(subtrair_2_q0), .in_3(not_2_out), .NEG(1'b0), .out_4(comparadorquatrobits_2_out_4));
  soma soma_1 (.in_1(1'b0), .in_2(in_1[0]), .in_3(in_2[0]), .SUM(out_3[0]), .CARRY(soma_1_carry));
  soma soma_2 (.in_1(soma_1_carry), .in_2(in_1[1]), .in_3(in_2[1]), .SUM(out_3[1]), .CARRY(soma_2_carry));
  soma soma_3 (.in_1(soma_2_carry), .in_2(in_1[2]), .in_3(in_2[2]), .SUM(out_3[2]), .CARRY(soma_3_carry));
  soma soma_4 (.in_1(soma_3_carry), .in_2(in_1[3]), .in_3(in_2[3]), .SUM(out_3[3]), .CARRY(out_3[4]));
  and and_1 (and_1_out, in_1[3], comparadorquatrobits_1_out_4[2]);
  and and_2 (and_2_out, in_2[3], comparadorquatrobits_2_out_4[2]);
  or or_1 (out_4, and_1_out, and_2_out);
endmodule

module varialvel (
  input  [3:0] in_1,
  input  CLK,
  input  CLEAR,
  input  ENABLE,
  output [3:0] out_5
);

  D_Flip_Flop d_ff_1 (.clk(CLK), .D(in_1[3]), .Q(out_5[3]), .en(ENABLE), .reset(CLEAR));  // open: Qn, preset
  D_Flip_Flop d_ff_2 (.clk(CLK), .D(in_1[2]), .Q(out_5[2]), .en(ENABLE), .reset(CLEAR));  // open: Qn, preset
  D_Flip_Flop d_ff_3 (.clk(CLK), .D(in_1[1]), .Q(out_5[1]), .en(ENABLE), .reset(CLEAR));  // open: Qn, preset
  D_Flip_Flop d_ff_4 (.clk(CLK), .D(in_1[0]), .Q(out_5[0]), .en(ENABLE), .reset(CLEAR));  // open: Qn, preset
  Hex_Digit_Display hex_digit_display_1 (.value(out_5));  // open: dp
endmodule

module passarChute (
  input  ENABLE,
  input  CLK,
  input  CLEAR,
  input  [3:0] in_4,
  input  [3:0] in_5,
  output [3:0] out_6,
  output [3:0] out_7,
  output out_8,
  output out_9
);

  varialvel varialvel_1 (.in_1(in_4), .CLK(CLK), .CLEAR(CLEAR), .ENABLE(ENABLE), .out_5(out_6));
  varialvel varialvel_2 (.in_1(in_5), .CLK(CLK), .CLEAR(CLEAR), .ENABLE(ENABLE), .out_5(out_7));

  assign out_8 = in_5[3];
  assign out_9 = in_4[3];
endmodule

module botao (
  input  PROXIMO,
  output CLK,
  output Q0,
  output Q1
);

  wire not_1_out;

  not not_1 (not_1_out, Q0);
  D_Flip_Flop d_ff_1 (.clk(PROXIMO), .D(not_1_out), .Q(Q0));  // open: Qn, preset, en, reset
  not not_2 (Q1, Q0);

  assign CLK = PROXIMO;
endmodule

module flipflopDescida (
  input  D,
  input  CLK,
  input  ENABLE,
  input  CLEAR,
  output Q
);

  wire and_1_out, and_2_out, and_3_out, nor_2_out, not_1_out, not_2_out, not_3_out, not_4_out, not_5_out;

  not not_1 (not_1_out, CLK);
  not not_2 (not_2_out, not_3_out);
  not not_3 (not_3_out, not_4_out);
  not not_4 (not_4_out, not_1_out);
  not not_5 (not_5_out, D);
  and and_1 (and_1_out, not_1_out, ENABLE, not_2_out);
  and and_2 (and_2_out, not_5_out, and_1_out);
  nor nor_1 (Q, and_2_out, CLEAR, nor_2_out);
  nor nor_2 (nor_2_out, Q, and_3_out);
  and and_3 (and_3_out, and_1_out, D);
endmodule

module aux_1 (
  input  [3:0] in_1,
  input  in_2,
  output [3:0] out_3
);

  wire not_1_out;

  not not_1 (not_1_out, in_2);
  and and_1 (out_3[0], ~not_1_out, in_1[0]);  // AND_Gate
  and and_2 (out_3[1], ~not_1_out, in_1[1]);  // AND_Gate
  and and_3 (out_3[2], ~not_1_out, in_1[2]);  // AND_Gate
  and and_4 (out_3[3], ~not_1_out, in_1[3]);  // AND_Gate
endmodule

module ponto (
  input  CLK,
  input  CLEAR,
  input  ENABLE,
  output [3:0] out_4
);

  wire somador_1_out_4;
  wire [4:0] somador_1_out_3;

  D_Flip_Flop d_ff_1 (.clk(CLK), .D(somador_1_out_3[3]), .Q(out_4[3]), .en(ENABLE), .reset(CLEAR));  // open: Qn, preset
  D_Flip_Flop d_ff_2 (.clk(CLK), .D(somador_1_out_3[2]), .Q(out_4[2]), .en(ENABLE), .reset(CLEAR));  // open: Qn, preset
  LED led_1 (.in(somador_1_out_4));
  somador somador_1 (.in_1(out_4), .in_2(4'b0001), .out_3(somador_1_out_3), .out_4(somador_1_out_4));
  D_Flip_Flop d_ff_3 (.clk(CLK), .D(somador_1_out_3[1]), .Q(out_4[1]), .en(ENABLE), .reset(CLEAR));  // open: Qn, preset
  D_Flip_Flop d_ff_4 (.clk(CLK), .D(somador_1_out_3[0]), .Q(out_4[0]), .en(ENABLE), .reset(CLEAR));  // open: Qn, preset
  Hex_Digit_Display hex_digit_display_1 (.value(out_4));  // open: dp
endmodule

module aux_2 (
  input  JOGADOR,
  input  in_2,
  output out_3,
  output out_4
);

  and and_1 (out_3, JOGADOR, in_2);
  and and_2 (out_4, ~JOGADOR, in_2);  // AND_Gate
endmodule

module aux_3 (
  input  in_1,
  input  in_2,
  input  in_3,
  input  in_4,
  input  in_5,
  input  in_6,
  input  in_7,
  input  in_8,
  output out_9,
  output out_10,
  output out_11,
  output out_12
);

  or or_1 (out_9, in_1, in_2);
  or or_2 (out_10, in_3, in_4);
  or or_3 (out_11, in_5, in_6);
  or or_4 (out_12, in_7, in_8);
endmodule

module aux_4 (
  input  D0,
  input  D1,
  input  D2,
  input  D3,
  input  D4,
  output Q0,
  output Q1,
  output Q2,
  output Q3
);

  wire and_1_out, and_2_out, and_3_out, and_4_out, and_5_out, and_6_out, and_7_out, and_8_out, and_9_out,
       and_10_out, not_1_out, not_2_out, not_3_out, not_4_out, not_5_out, not_6_out, not_7_out, not_8_out;

  and and_1 (and_1_out, D3, D4);
  and and_2 (and_2_out, D2, D4);
  and and_3 (and_3_out, D1, D4);
  not not_1 (not_1_out, D1);
  not not_2 (not_2_out, D1);
  not not_3 (not_3_out, D2);
  not not_4 (not_4_out, D3);
  not not_5 (not_5_out, D4);
  not not_6 (not_6_out, D2);
  not not_7 (not_7_out, D3);
  not not_8 (not_8_out, D4);
  or or_1 (Q0, and_1_out, and_2_out, and_3_out, D0);
  and and_4 (and_4_out, not_1_out, D3, D4);
  and and_5 (and_5_out, not_2_out, D2, D4);
  and and_6 (and_6_out, D1, not_3_out, not_4_out);
  and and_7 (and_7_out, D1, not_5_out);
  and and_8 (and_8_out, not_6_out, D3, D4);
  and and_9 (and_9_out, D2, not_7_out);
  and and_10 (and_10_out, D2, not_8_out);
  or or_2 (Q1, and_4_out, and_5_out, and_6_out, and_7_out);
  or or_3 (Q2, and_8_out, and_9_out, and_10_out);

  assign Q3 = D3;
endmodule

module decrementarUnidade (
  input  D0,
  input  D1,
  input  D2,
  input  D3,
  output Q0,
  output Q1,
  output Q2,
  output Q3,
  output SS,
  output zz
);

  wire and_1_out, and_2_out, and_3_out, and_4_out, and_5_out, and_6_out, and_8_out, and_9_out, not_1_out,
       not_2_out, not_3_out, not_4_out, not_5_out, not_6_out, not_7_out, not_8_out, not_10_out, not_11_out,
       not_12_out, not_13_out;

  not not_1 (not_1_out, D0);
  not not_2 (not_2_out, D1);
  not not_3 (not_3_out, D2);
  not not_4 (not_4_out, D3);
  and and_1 (and_1_out, D1, D3);
  and and_2 (and_2_out, D1, D2);
  and and_3 (and_3_out, D0, not_5_out);
  not not_5 (not_5_out, D3);
  and and_4 (and_4_out, D2, D3);
  and and_5 (and_5_out, D1, not_6_out, not_7_out);
  not not_6 (not_6_out, D2);
  not not_7 (not_7_out, D3);
  and and_6 (and_6_out, D0, not_8_out);
  not not_8 (not_8_out, D3);
  not not_9 (Q3, D3);
  and and_7 (SS, D0, D3);
  not not_10 (not_10_out, D0);
  not not_11 (not_11_out, D1);
  not not_12 (not_12_out, D2);
  not not_13 (not_13_out, D3);
  and and_8 (and_8_out, not_1_out, not_2_out, not_3_out, not_4_out);
  or or_1 (Q0, and_8_out, and_9_out);
  and and_9 (and_9_out, D0, D3);
  or or_2 (Q1, and_1_out, and_2_out, and_3_out);
  or or_3 (Q2, and_4_out, and_5_out, and_6_out);
  and and_10 (zz, not_10_out, not_11_out, not_12_out, not_13_out);
endmodule

module decrementarDezena (
  input  D0,
  input  D1,
  input  D2,
  input  D3,
  output Q0,
  output Q1,
  output Q2,
  output Q3,
  output SS,
  output zz
);

  wire and_1_out, and_2_out, and_3_out, and_4_out, and_5_out, not_1_out, not_2_out, not_3_out, not_4_out,
       not_5_out, not_6_out, not_8_out, not_9_out, not_10_out, not_11_out;

  not not_1 (not_1_out, D1);
  and and_1 (and_1_out, not_1_out, not_2_out, not_3_out);
  not not_2 (not_2_out, D2);
  not not_3 (not_3_out, D3);
  and and_2 (and_2_out, D1, D3);
  and and_3 (and_3_out, D2, D3);
  not not_4 (not_4_out, D2);
  and and_4 (and_4_out, D1, not_4_out, not_5_out);
  not not_5 (not_5_out, D3);
  and and_5 (and_5_out, D0, not_6_out);
  not not_6 (not_6_out, D3);
  not not_7 (Q3, D3);
  and and_6 (SS, D1, D3);
  not not_8 (not_8_out, D0);
  not not_9 (not_9_out, D1);
  not not_10 (not_10_out, D2);
  not not_11 (not_11_out, D3);
  or or_1 (Q1, and_1_out, and_2_out);
  or or_2 (Q2, and_3_out, and_4_out, and_5_out);
  and and_7 (zz, not_8_out, not_9_out, not_10_out, not_11_out);

  assign Q0 = 1'b0;
endmodule

// aux[4]
module comparadorCincoBits (
  input  [4:0] CHUTE,
  input  in_2,
  input  [4:0] in_3,
  output [2:0] out_4
);

  wire _0_2_out, _0_out, _1_2_out, _1_out, _2_2_out, _2_out, _3_2_out, _3_out, _4_2_out, _4_out, MAIOR_out,
       MENOR_out, xor_1_out, xor_2_out;

  xnor _0 (_0_out, in_3[0], CHUTE[0]);
  xnor _1 (_1_out, in_3[1], CHUTE[1]);
  xnor _2 (_2_out, in_3[2], CHUTE[2]);
  xnor _3 (_3_out, in_3[3], CHUTE[3]);
  xnor _4 (_4_out, in_3[4], CHUTE[4]);
  and IGUAL (out_4[1], _0_out, _1_out, _2_out, _3_out, _4_out);
  and _0_2 (_0_2_out, CHUTE[0], _1_out, _2_out, _3_out, ~in_3[0], _4_out);  // AND_Gate
  and _1_2 (_1_2_out, CHUTE[1], ~in_3[1], _4_out, _2_out, _3_out);  // AND_Gate
  and _2_2 (_2_2_out, CHUTE[2], ~in_3[2], _3_out, _4_out);  // AND_Gate
  and _3_2 (_3_2_out, CHUTE[3], ~in_3[3], _4_out);  // AND_Gate
  and _4_2 (_4_2_out, CHUTE[4], ~in_3[4]);  // AND_Gate
  or MAIOR (MAIOR_out, _0_2_out, _1_2_out, _4_2_out, _2_2_out, _3_2_out);
  nor MENOR (MENOR_out, out_4[1], MAIOR_out);
  ExactlyOne xor_1 (.out(xor_1_out), .in0(in_2), .in1(out_4[1]), .in2(MENOR_out));
  ExactlyOne xor_2 (.out(xor_2_out), .in0(in_2), .in1(out_4[1]), .in2(MAIOR_out));
  and and_1 (out_4[0], ~out_4[1], xor_1_out);  // AND_Gate
  and and_2 (out_4[2], ~out_4[1], xor_2_out);  // AND_Gate
endmodule

module visorNegado (
  input  D0,
  input  D1,
  input  D2,
  input  D3,
  output Q0,
  output Q1,
  output Q2,
  output Q3
);

  wire and_1_out, and_2_out, and_3_out, and_4_out, and_5_out, and_6_out, and_7_out, not_1_out, not_2_out,
       not_3_out, not_4_out, not_5_out, not_6_out, not_7_out, not_8_out, not_9_out, not_10_out, not_11_out;

  not not_1 (not_1_out, D1);
  not not_2 (not_2_out, D2);
  not not_3 (not_3_out, D3);
  not not_4 (not_4_out, D0);
  and and_1 (and_1_out, not_4_out, D1);
  and and_2 (and_2_out, D1, not_5_out, not_6_out);
  not not_5 (not_5_out, D2);
  not not_6 (not_6_out, D3);
  not not_7 (not_7_out, D1);
  and and_3 (and_3_out, D0, not_7_out, D3);
  and and_4 (and_4_out, D0, not_8_out, D2);
  not not_8 (not_8_out, D1);
  not not_9 (not_9_out, D0);
  and and_5 (and_5_out, not_9_out, D2);
  and and_6 (and_6_out, D2, not_10_out);
  not not_10 (not_10_out, D3);
  not not_11 (not_11_out, D2);
  and and_7 (and_7_out, D0, not_11_out, D3);
  and and_8 (Q0, D0, not_1_out, not_2_out, not_3_out);
  or or_1 (Q1, and_1_out, and_2_out, and_3_out, and_4_out);
  or or_2 (Q2, and_5_out, and_6_out, and_7_out);

  assign Q3 = D3;
endmodule

module verificador (
  input  PROX,
  input  CLEAR,
  input  ENABLE,
  output _0,
  output _1,
  output _2,
  output _3
);

  wire aux_5_1_q0, aux_5_1_q1, d_ff_1_q, d_ff_2_q;

  D_Flip_Flop d_ff_1 (.clk(PROX), .D(aux_5_1_q1), .Q(d_ff_1_q), .en(ENABLE), .reset(CLEAR));  // open: Qn, preset
  aux_5 aux_5_1 (.D0(d_ff_2_q), .D1(d_ff_1_q), .Q0(aux_5_1_q0), .Q1(aux_5_1_q1));
  D_Flip_Flop d_ff_2 (.clk(PROX), .D(aux_5_1_q0), .Q(d_ff_2_q), .en(ENABLE), .reset(CLEAR));  // open: Qn, preset
  and and_1 (_0, ~d_ff_2_q, ~d_ff_1_q);  // AND_Gate
  and and_2 (_1, ~d_ff_2_q, d_ff_1_q);  // AND_Gate
  and and_3 (_3, d_ff_2_q, d_ff_1_q);
  and and_4 (_2, d_ff_2_q, ~d_ff_1_q);  // AND_Gate
endmodule

module aux_5 (
  input  D0,
  input  D1,
  output Q0,
  output Q1
);

  wire and_1_out, and_2_out, not_1_out, not_2_out;

  not not_1 (not_1_out, D0);
  not not_2 (not_2_out, D1);
  not not_3 (Q1, D1);
  and and_1 (and_1_out, not_1_out, D1);
  and and_2 (and_2_out, D0, not_2_out);
  or or_1 (Q0, and_1_out, and_2_out);
endmodule

module troca (
  input  clk,
  input  RESET,
  input  PRESET,
  output saida
);

  wire not_1_out;

  not not_1 (not_1_out, saida);
  D_Flip_Flop d_ff_1 (.clk(clk), .D(not_1_out), .Q(saida), .preset(PRESET), .reset(RESET));  // open: Qn, en
endmodule

module displayFinal (
  input  [3:0] in_1,
  output out_2,
  output [3:0] out_3,
  output [3:0] out_4
);

  wire [3:0] visornegado_1_q3;

  visorNegado visornegado_1 (
    .D0(in_1[3]), .D1(in_1[2]), .D2(in_1[1]), .D3(in_1[0]), .Q0(visornegado_1_q3[3]),
    .Q1(visornegado_1_q3[2]), .Q2(visornegado_1_q3[1]), .Q3(visornegado_1_q3[0]));
  display_0_f display_0_f_1 (.in_1(visornegado_1_q3), .SUPERIOR(out_4), .INFERIOR(out_3));

  assign out_2 = in_1[3];
endmodule

module multiplexJogadores (
  input  [3:0] in_1,
  input  [3:0] in_2,
  input  in_3,
  output [3:0] out_4
);

  wire [3:0] and_4_out, and_5_out;

  and and_1 (and_4_out[3], in_1[3], in_3);
  and and_2 (and_4_out[2], in_1[2], in_3);
  and and_3 (and_4_out[1], in_1[1], in_3);
  and and_4 (and_4_out[0], in_1[0], in_3);
  and and_5 (and_5_out[0], ~in_3, in_2[0]);  // AND_Gate
  and and_6 (and_5_out[1], ~in_3, in_2[1]);  // AND_Gate
  and and_7 (and_5_out[2], ~in_3, in_2[2]);  // AND_Gate
  and and_8 (and_5_out[3], ~in_3, in_2[3]);  // AND_Gate
  assign out_4 = and_4_out | and_5_out;  // OR_Gate or_1, 4 bits wide
endmodule

module APAGAR (
  input  [3:0] in_1,
  input  [3:0] in_2
);

  wire CHUTE_out, core_1__1, core_1__2, core_1_ligado, core_1_negx, core_1_negy, core_1_out_12,
       core_1_out_13, core_1_out_14, core_1_x, core_1_y, displayfinal_1_out_2, displayfinal_2_out_2, LIG_out,
       PROXIMO_out, ZERA_out;
  wire [3:0] core_1_display_a___x, core_1_display_a___y, core_1_display_b___x, core_1_display_b___y,
       core_1_pontoa, core_1_pontob, displayfinal_1_out_3, displayfinal_1_out_4, displayfinal_2_out_3,
       displayfinal_2_out_4;

  _7_Segment_Display u_7_segment_display_1 (.g(displayfinal_1_out_2));  // open: f, a, b, e, d, c, dp
  LED _1 (.in(core_1__1));
  displayFinal displayfinal_1 (
    .in_1(in_1), .out_2(displayfinal_1_out_2), .out_3(displayfinal_1_out_3), .out_4(displayfinal_1_out_4));
  _7_Segment_Display u_7_segment_display_2 (
    .g(displayfinal_1_out_4[3]), .f(displayfinal_1_out_4[2]), .a(displayfinal_1_out_4[1]),
    .b(displayfinal_1_out_4[0]), .e(displayfinal_1_out_3[3]), .d(displayfinal_1_out_3[2]),
    .c(displayfinal_1_out_3[1]), .dp(displayfinal_1_out_3[0]));
  Button PROXIMO (.out(PROXIMO_out));
  Button CHUTE (.out(CHUTE_out));
  Button ZERA (.out(ZERA_out));
  Button LIG (.out(LIG_out));
  _7_Segment_Display u_7_segment_display_3 (.g(core_1_negx));  // open: f, a, b, e, d, c, dp
  Hex_Digit_Display hex_digit_display_1 (.value(core_1_pontoa));  // open: dp
  LED LIGADO (.in(core_1_ligado));
  LED X (.in(core_1_x));
  _7_Segment_Display u_7_segment_display_4 (
    .g(core_1_display_b___x[3]), .f(core_1_display_b___x[2]), .a(core_1_display_b___x[1]),
    .b(core_1_display_b___x[0]), .e(core_1_display_a___x[3]), .d(core_1_display_a___x[2]),
    .c(core_1_display_a___x[1]), .dp(core_1_display_a___x[0]));
  Hex_Digit_Display hex_digit_display_2 (.value(core_1_pontob));  // open: dp
  LED led (.in(core_1_out_12));
  CORE core_1 (
    .PROXIMO(PROXIMO_out), .CHUTE(CHUTE_out), .CLEAR(ZERA_out), .ENABLE(LIG_out), .pontoA(core_1_pontoa),
    .pontoB(core_1_pontob), .ENTRADA(in_1), .ENTRADA_2(in_2), .ligado(core_1_ligado), ._1(core_1__1),
    ._2(core_1__2), .X(core_1_x), .Y(core_1_y), .negX(core_1_negx), .DISPLAY_A___x(core_1_display_a___x),
    .DISPLAY_B___x(core_1_display_b___x), .negY(core_1_negy), .DISPLAY_A___Y(core_1_display_a___y),
    .DISPLAY_B___Y(core_1_display_b___y), .out_12(core_1_out_12), .out_13(core_1_out_13),
    .out_14(core_1_out_14));  // open: out_9, RESET, PRESET
  LED Y (.in(core_1_y));
  _7_Segment_Display u_7_segment_display_5 (.g(core_1_negy));  // open: f, a, b, e, d, c, dp
  LED led_2 (.in(core_1_out_13));
  LED led_3 (.in(core_1_out_14));
  _7_Segment_Display u_7_segment_display_6 (
    .g(core_1_display_b___y[3]), .f(core_1_display_b___y[2]), .a(core_1_display_b___y[1]),
    .b(core_1_display_b___y[0]), .e(core_1_display_a___y[3]), .d(core_1_display_a___y[2]),
    .c(core_1_display_a___y[1]), .dp(core_1_display_a___y[0]));
  _7_Segment_Display u_7_segment_display_7 (.g(displayfinal_2_out_2));  // open: f, a, b, e, d, c, dp
  LED _2 (.in(core_1__2));
  displayFinal displayfinal_2 (
    .in_1(in_2), .out_2(displayfinal_2_out_2), .out_3(displayfinal_2_out_3), .out_4(displayfinal_2_out_4));
  _7_Segment_Display u_7_segment_display_8 (
    .g(displayfinal_2_out_4[3]), .f(displayfinal_2_out_4[2]), .a(displayfinal_2_out_4[1]),
    .b(displayfinal_2_out_4[0]), .e(displayfinal_2_out_3[3]), .d(displayfinal_2_out_3[2]),
    .c(displayfinal_2_out_3[1]), .dp(displayfinal_2_out_3[0]));
endmodule

module coreLeds (
  input  ENABLE,
  input  JOGADOR,
  input  _1,
  input  _2,
  output ligado,
  output _1_2,
  output _2_2,
  output X,
  output Y
);

  and and_1 (_1_2, ENABLE, JOGADOR);
  and and_2 (_2_2, ENABLE, ~JOGADOR);  // AND_Gate
  and and_3 (Y, ENABLE, _2);
  and and_4 (X, ENABLE, _1);

  assign ligado = ENABLE;
endmodule

module core_3 (
  input  RESET,
  input  PRESET,
  input  _3,
  input  comp1,
  input  comp2,
  input  _2,
  input  clear,
  output [3:0] pontoA,
  output [3:0] pontoB,
  output jogador
);

  wire and_1_out, and_2_out, aux_2_1_out_3, aux_2_1_out_4;

  and and_1 (and_1_out, comp1, comp2);
  and and_2 (and_2_out, and_1_out, _2);
  troca troca_1 (.clk(_3), .RESET(RESET), .PRESET(PRESET), .saida(jogador));
  aux_2 aux_2_1 (.in_2(and_2_out), .JOGADOR(jogador), .out_3(aux_2_1_out_3), .out_4(aux_2_1_out_4));
  ponto PONTO_B (.CLK(aux_2_1_out_4), .CLEAR(clear), .ENABLE(_2), .out_4(pontoB));
  ponto PONTo_A (.CLK(aux_2_1_out_3), .CLEAR(clear), .ENABLE(_2), .out_4(pontoA));
endmodule

module core_2 (
  input  clear,
  input  _3,
  input  [3:0] valor1,
  input  [3:0] valor2,
  input  enable,
  input  _2,
  input  [3:0] in_7,
  input  [3:0] in_8,
  output comp1,
  output comp2,
  output menor,
  output igual,
  output maior
);

  wire or_1_out, passarchute_1_out_8, passarchute_1_out_9, somador_1_out_4, somador_2_out_4, xor_1_out;
  wire [2:0] comparadorcincobits_1_out_4, comparadorquatrobits_1_out_4, comparadorquatrobits_2_out_4;
  wire [3:0] passarchute_1_out_6, passarchute_1_out_7;
  wire [4:0] somador_1_out_3, somador_2_out_3;

  or or_1 (or_1_out, clear, _3);
  comparadorQuatroBits comparadorquatrobits_1 (
    .CHUTE(passarchute_1_out_6), .in_3(valor1), .NEG(passarchute_1_out_8),
    .out_4({comparadorquatrobits_1_out_4[2], comp1, comparadorquatrobits_1_out_4[0]}));
  passarChute passarchute_1 (
    .ENABLE(enable), .CLK(_2), .CLEAR(or_1_out), .in_4(in_7), .in_5(in_8), .out_6(passarchute_1_out_6),
    .out_7(passarchute_1_out_7), .out_8(passarchute_1_out_8), .out_9(passarchute_1_out_9));
  comparadorQuatroBits comparadorquatrobits_2 (
    .CHUTE(passarchute_1_out_7), .in_3(valor2), .NEG(passarchute_1_out_9),
    .out_4({comparadorquatrobits_2_out_4[2], comp2, comparadorquatrobits_2_out_4[0]}));
  somador somador_1 (
    .in_1(passarchute_1_out_6), .in_2(passarchute_1_out_7), .out_3(somador_1_out_3), .out_4(somador_1_out_4));
  somador somador_2 (.in_1(valor2), .in_2(valor1), .out_3(somador_2_out_3), .out_4(somador_2_out_4));
  xor xor_1 (xor_1_out, somador_1_out_4, somador_2_out_4);
  comparadorCincoBits comparadorcincobits_1 (
    .CHUTE(somador_1_out_3), .in_2(xor_1_out), .in_3(somador_2_out_3), .out_4(comparadorcincobits_1_out_4));
  and and_1 (menor, _2, comparadorcincobits_1_out_4[0]);
  and and_2 (igual, _2, comparadorcincobits_1_out_4[1]);
  and and_3 (maior, _2, comparadorcincobits_1_out_4[2]);
endmodule

module afirmador (
  input  [3:0] in_1
);

  wire [3:0] not_1_out;

  assign not_1_out = ~in_1;  // NOT_Gate not_1, 4 bits wide
endmodule

module sub (
  input  in_1,
  input  in_2,
  input  in_3,
  output out_4,
  output out_5
);

  wire and_1_out, and_2_out, and_3_out, xor_1_out;

  and and_1 (and_1_out, in_2, in_3);
  and and_2 (and_2_out, ~in_1, in_3);  // AND_Gate
  and and_3 (and_3_out, ~in_1, in_2);  // AND_Gate
  xor xor_1 (xor_1_out, in_1, in_2);
  xor xor_2 (out_4, xor_1_out, in_3);
  or or_1 (out_5, and_1_out, and_2_out, and_3_out);
endmodule

module subtrador (
);

  wire sub_2_out_5, sub_3_out_5, sub_4_out_5;

  sub sub_1 (.in_3(sub_2_out_5));  // open: in_1, in_2, out_4, out_5
  sub sub_2 (.in_3(sub_3_out_5), .out_5(sub_2_out_5));  // open: in_1, in_2, out_4
  sub sub_3 (.in_3(sub_4_out_5), .out_5(sub_3_out_5));  // open: in_1, in_2, out_4
  sub sub_4 (.in_3(1'b0), .out_5(sub_4_out_5));  // open: in_1, in_2, out_4
endmodule

module SUBTRAIR (
  input  D0,
  input  D1,
  input  D2,
  input  D3,
  output Q0,
  output Q1,
  output Q2,
  output Q3
);

  wire and_1_out, and_2_out, and_3_out, and_4_out, and_5_out, and_6_out, and_7_out, and_8_out, and_9_out,
       and_10_out, and_11_out, and_12_out, not_1_out, not_2_out, not_3_out, not_4_out, not_5_out, not_6_out,
       not_7_out, not_8_out, not_9_out, not_10_out;

  and and_1 (and_1_out, D0, D3);
  and and_2 (and_2_out, D0, D2);
  and and_3 (and_3_out, D0, D1);
  not not_1 (not_1_out, D1);
  not not_2 (not_2_out, D2);
  not not_3 (not_3_out, D3);
  and and_4 (and_4_out, D2, D3);
  and and_5 (and_5_out, D1, not_4_out, not_5_out);
  not not_4 (not_4_out, D2);
  not not_5 (not_5_out, D3);
  not not_6 (not_6_out, D2);
  and and_6 (and_6_out, D0, not_6_out, not_7_out);
  not not_7 (not_7_out, D3);
  and and_7 (and_7_out, D2, not_8_out);
  not not_8 (not_8_out, D3);
  and and_8 (and_8_out, D1, not_9_out);
  not not_9 (not_9_out, D3);
  and and_9 (and_9_out, D0, not_10_out);
  not not_10 (not_10_out, D3);
  or or_1 (Q0, and_1_out, and_2_out, and_3_out);
  and and_10 (and_10_out, D1, D3);
  and and_11 (and_11_out, D1, D2);
  or or_2 (Q1, and_10_out, and_11_out, and_12_out);
  and and_12 (and_12_out, D0, not_1_out, not_2_out, not_3_out);
  or or_3 (Q2, and_4_out, and_5_out, and_6_out);
  or or_4 (Q3, and_7_out, and_8_out, and_9_out);
endmodule
