// Logisim project PROJETO2 - CD.circ as structural Verilog: 6 circuits, main circuit FLIPFLOPD SUBIDA
module main (
  input  ENABLE,
  input  CLEAR,
  input  CLK
);

  wire contuni_1_clk_prox;
  wire [3:0] contdec_1_out_4, contuni_1_out_4;

  Hex_Digit_Display hex_digit_display_1 (.value(contdec_1_out_4));  // open: dp
  Hex_Digit_Display hex_digit_display_2 (.value(contuni_1_out_4));  // open: dp
  CONTDEC contdec_1 (
    .CLK(contuni_1_clk_prox), .CLEAR(CLEAR), .ENABLE(ENABLE), .out_4(contdec_1_out_4));  // open: CLK_PROX
  CONTUNI contuni_1 (.CLK_PROX(contuni_1_clk_prox), .CLK(CLK), .CLEAR(CLEAR), .ENABLE(ENABLE), .out_4(contuni_1_out_4));
endmodule

module FLIPFLOPD_SUBIDA (
  input  D,
  input  CLK,
  input  ENABLE,
  input  CLEAR,
  output Q
);

  wire and_1_out, and_2_out, and_3_out, nor_2_out, not_1_out, not_2_out, not_3_out, not_4_out;

  not not_1 (not_1_out, not_2_out);
  not not_2 (not_2_out, CLK);
  not not_3 (not_3_out, not_1_out);
  and and_1 (and_1_out, CLK, ENABLE, not_3_out);
  not not_4 (not_4_out, D);
  and and_2 (and_2_out, not_4_out, and_1_out);
  and and_3 (and_3_out, and_1_out, D);
  nor nor_1 (Q, and_2_out, CLEAR, nor_2_out);
  nor nor_2 (nor_2_out, Q, and_3_out);
endmodule

// 9-0
module CONTUNI (
  input  CLK,
  input  CLEAR,
  input  ENABLE,
  output [3:0] out_4,
  output CLK_PROX
);

  wire conversor09_1_q0, conversor09_1_q1, conversor09_1_q2, conversor09_1_q3;

  FLIPFLOPD_SUBIDA flipflopd_subida_1 (.D(conversor09_1_q0), .CLK(CLK), .ENABLE(ENABLE), .CLEAR(CLEAR), .Q(out_4[3]));
  FLIPFLOPD_SUBIDA flipflopd_subida_2 (.D(conversor09_1_q1), .CLK(CLK), .ENABLE(ENABLE), .CLEAR(CLEAR), .Q(out_4[2]));
  FLIPFLOPD_SUBIDA flipflopd_subida_3 (.D(conversor09_1_q2), .CLK(CLK), .ENABLE(ENABLE), .CLEAR(CLEAR), .Q(out_4[1]));
  CONVERSOR09 conversor09_1 (
    .D0(out_4[3]), .D1(out_4[2]), .D2(out_4[1]), .D3(out_4[0]), .Q0(conversor09_1_q0), .Q1(conversor09_1_q1),
    .Q2(conversor09_1_q2), .Q3(conversor09_1_q3), .SS(CLK_PROX));
  FLIPFLOPD_SUBIDA flipflopd_subida_4 (.D(conversor09_1_q3), .CLK(CLK), .ENABLE(ENABLE), .CLEAR(CLEAR), .Q(out_4[0]));
  Hex_Digit_Display hex_digit_display_1 (.value(out_4));  // open: dp
endmodule

// 5-0
module CONTDEC (
  input  CLK,
  input  CLEAR,
  input  ENABLE,
  output [3:0] out_4,
  output CLK_PROX
);

  wire conversor05_1_q0, conversor05_1_q1, conversor05_1_q2, conversor05_1_q3;

  FLIPFLOPD_SUBIDA flipflopd_subida_1 (.D(conversor05_1_q0), .CLK(CLK), .ENABLE(ENABLE), .CLEAR(CLEAR), .Q(out_4[3]));
  FLIPFLOPD_SUBIDA flipflopd_subida_2 (.D(conversor05_1_q1), .CLK(CLK), .ENABLE(ENABLE), .CLEAR(CLEAR), .Q(out_4[2]));
  FLIPFLOPD_SUBIDA flipflopd_subida_3 (.D(conversor05_1_q2), .CLK(CLK), .ENABLE(ENABLE), .CLEAR(CLEAR), .Q(out_4[1]));
  CONVERSOR05 conversor05_1 (
    .D0(out_4[3]), .D1(out_4[2]), .D2(out_4[1]), .D3(out_4[0]), .Q0(conversor05_1_q0), .Q1(conversor05_1_q1),
    .Q2(conversor05_1_q2), .Q3(conversor05_1_q3), .SS(CLK_PROX));
  FLIPFLOPD_SUBIDA flipflopd_subida_4 (.D(conversor05_1_q3), .CLK(CLK), .ENABLE(ENABLE), .CLEAR(CLEAR), .Q(out_4[0]));
  Hex_Digit_Display hex_digit_display_1 (.value(out_4));  // open: dp
endmodule

module CONVERSOR09 (
  input  D0,
  input  D1,
  input  D2,
  input  D3,
  output Q0,
  output Q1,
  output Q2,
  output Q3,
  output SS
);

  wire and_1_out, and_2_out, and_3_out, and_4_out, and_5_out, and_6_out, and_7_out, and_8_out, not_1_out,
       not_2_out, not_3_out, not_4_out, not_5_out, not_6_out, not_7_out, not_8_out, not_10_out, not_11_out,
       not_12_out, not_13_out;

  not not_1 (not_1_out, D0);
  not not_2 (not_2_out, D1);
  not not_3 (not_3_out, D2);
  not not_4 (not_4_out, D3);
  and and_1 (and_1_out, D1, D3);
  and and_2 (and_2_out, D1, D2);
  and and_3 (and_3_out, D0, not_5_out);
  not not_5 (not_5_out, D3);
  and and_4 (and_4_out, D2, D3);
  and and_5 (and_5_out, D1, not_6_out, not_7_out);
  not not_6 (not_6_out, D2);
  not not_7 (not_7_out, D3);
  and and_6 (and_6_out, D0, not_8_out);
  not not_8 (not_8_out, D3);
  not not_9 (Q3, D3);
  not not_10 (not_10_out, D0);
  not not_11 (not_11_out, D1);
  not not_12 (not_12_out, D2);
  not not_13 (not_13_out, D3);
  and and_7 (and_7_out, not_1_out, not_2_out, not_3_out, not_4_out);
  or or_1 (Q0, and_7_out, and_8_out);
  and and_8 (and_8_out, D0, D3);
  or or_2 (Q1, and_1_out, and_2_out, and_3_out);
  or or_3 (Q2, and_4_out, and_5_out, and_6_out);
  and and_9 (SS, not_10_out, not_11_out, not_12_out, not_13_out);
endmodule

module CONVERSOR05 (
  input  D0,
  input  D1,
  input  D2,
  input  D3,
  output Q0,
  output Q1,
  output Q2,
  output Q3,
  output SS
);

  wire and_2_out, and_3_out, and_4_out, and_5_out, and_6_out, and_7_out, not_1_out, not_2_out, not_3_out,
       not_4_out, not_5_out, not_6_out, not_7_out, not_8_out;

  and and_1 (Q0, D1, D2);
  not not_1 (not_1_out, D1);
  and and_2 (and_2_out, not_1_out, not_2_out, not_3_out);
  not not_2 (not_2_out, D2);
  not not_3 (not_3_out, D3);
  and and_3 (and_3_out, D1, D3);
  and and_4 (and_4_out, D2, D3);
  and and_5 (and_5_out, D1, not_4_out);
  not not_4 (not_4_out, D3);
  not not_5 (not_5_out, D3);
  and and_6 (and_6_out, D1, D2);
  not not_6 (not_6_out, D1);
  and and_7 (and_7_out, not_6_out, not_7_out, not_8_out);
  not not_7 (not_7_out, D2);
  not not_8 (not_8_out, D3);
  or or_1 (Q1, and_2_out, and_3_out, D0);
  or or_2 (Q2, and_4_out, and_5_out, D0);
  or or_3 (Q3, not_5_out, and_6_out);
  or or_4 (SS, and_7_out, D0);
endmodule
